# Fritzing sketch CLController (saved by Fritzing 0.9.3b)
circuit board: 12.3395cm x 6.62885cm
breadboards: 2

parts:
  Huzzah_ESP8266 = Adafruit HUZZAH ESP8266 [part_number="Adafruit #2471"]
  Q1 = ULN2803 Darlington Array
  R1 = Resistor [tolerance=±5% resistance=4.7k package=THT]
  LED1 = LED - 5mm [color="Green (565nm)" package="5 mm [THT]"]
  Q2 = ULN2803 Darlington Array
  LED2 = LED - 5mm [color="Yellow (595nm)" package="5 mm [THT]"]
  J2 = shrouded pin header, 10 pins [form="♂ (shrouded male)"]
  J3 = shrouded pin header, 10 pins [form="♂ (shrouded male)"]
  IC1 = MCP23017 I2C I/O Expander
  J5 = male pin header, 6 pins [form="♂ (male)"]
  C1 = Ceramic Capacitor [capacitance=100nF package="100 mil [THT, multilayer]"]
  C2 = Ceramic Capacitor [capacitance=100nF package="100 mil [THT, multilayer]"]
  C3 = Ceramic Capacitor [capacitance=100nF package="100 mil [THT, multilayer]"]
  C4 = Ceramic Capacitor [capacitance=100nF package="100 mil [THT, multilayer]"]
  J1 = screw terminal, 2 pins
  J6 = screw terminal, 2 pins
  LED3 = LED - 5mm [color="Red (633nm)" package="5 mm [THT]"]
  R2 = Resistor [tolerance=±5% resistance=150 package=THT]

nets:
  N1: Huzzah_ESP8266.TX, J5.pin2
  N2: Huzzah_ESP8266.RX, J5.pin3
  N3: Huzzah_ESP8266.VIN, Q1.COMMON, Q2.COMMON, J2.pin1, J3.pin1, J5.pin4, C1.1, C3.0, C4.0, J1.pin2, LED3.anode
  GND: Huzzah_ESP8266.GND, Q1.GND, LED1.cathode, Q2.GND, LED2.cathode, J2.pin10, J3.pin10, IC1.VSS, IC1.A0, IC1.A1, IC1.A2, J5.pin6, C1.0, C2.1, C3.1, C4.1, J1.pin1, R2.Pin_0
  N4: Huzzah_ESP8266.GPIO16, LED1.anode
  N5: Huzzah_ESP8266.GPIO14, LED2.anode
  N6: Huzzah_ESP8266.GPIO12, R1.Pin_0, IC1.VDD, C2.0
  N7: Huzzah_ESP8266.GPIO4, IC1.SDA, J6.pin1
  N8: Huzzah_ESP8266.GPIO5, IC1.SCL, J6.pin2
  N9: Q1.I1, IC1.GPA0
  N10: Q1.I2, IC1.GPA1
  N11: Q1.I3, IC1.GPA2
  N12: Q1.I4, IC1.GPA3
  N13: Q1.I5, IC1.GPA4
  N14: Q1.I6, IC1.GPA5
  N15: Q1.I7, IC1.GPA6
  N16: Q1.I8, IC1.GPA7
  N17: Q1.O8, J3.pin9
  N18: Q1.O7, J3.pin8
  N19: Q1.O6, J3.pin7
  N20: Q1.O5, J3.pin6
  N21: Q1.O4, J3.pin5
  N22: Q1.O3, J3.pin4
  N23: Q1.O2, J3.pin3
  N24: Q1.O1, J3.pin2
  N25: R1.Pin_1, IC1.RESET
  N26: Q2.I1, IC1.GPB0
  N27: Q2.I2, IC1.GPB1
  N28: Q2.I3, IC1.GPB2
  N29: Q2.I4, IC1.GPB3
  N30: Q2.I5, IC1.GPB4
  N31: Q2.I6, IC1.GPB5
  N32: Q2.I7, IC1.GPB6
  N33: Q2.I8, IC1.GPB7
  N34: Q2.O8, J2.pin9
  N35: Q2.O7, J2.pin8
  N36: Q2.O6, J2.pin7
  N37: Q2.O5, J2.pin6
  N38: Q2.O4, J2.pin5
  N39: Q2.O3, J2.pin4
  N40: Q2.O2, J2.pin3
  N41: Q2.O1, J2.pin2
  N42: LED3.cathode, R2.Pin_1

notes:
  5VDC 3.0A
  +
  -
  Act
  IoT Christmas Lights Controller
  CLController Rev 1.1
  Copyright (c) 2022 Cyrus Brunner
  www.cyrusbuilt.net
  Run
  FAB 00101 ASSY 00102
  GND
  VIN
  RX
  TX
  Port B
  Port A
  CLController, IoT Christmas Lights Controller.  Designer: Cyrus Brunner, 1.1
  +5V DC 1.0A
  COM
  ACT
  RUN
  +5V
  REL 8
  REL 7
  REL 6
  REL 5
  REL 4
  REL 3
  REL 2
  REL 1
  SCL
  SDA
  MCP23017
  ULN2803
  RS-232
  PWR

custom parts:
  Adafruit HUZZAH ESP8266: Add Internet to your next project with an adorable, bite-sized WiFi microcontroller, at a price you like! The ESP8266 processor from Espressif is an 80 MHz microcontroller with a full WiFi front-end (both as client and access point) and TCP/IP stack with DNS support as well. While this chip has been very popular, its also been very difficult to use. Most of the low cost modules are not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
  ULN2803 Darlington Array: ULN2803 Darlington Transistor Array with Flyback Protection
  MCP23017 I2C I/O Expander: The MCP23017 uses two i2c pins (these can be shared with other i2c devices), and in exchange gives you 16 general purpose pins. You can set each of 16 pins to be input, output, input with a pullup or open drain. There's even the ability to get an interrupt via an external pin when any of the inputs change so you don't have to keep polling the chip.
