# Fritzing sketch ExpansionModule (saved by Fritzing 0.9.3b)
circuit board: 10.9567cm x 7.34938cm
breadboards: 2

parts:
  IC1 = MCP23017 I2C I/O Expander
  Q1 = ULN2803 Darlington Array
  Q2 = ULN2803 Darlington Array
  C1 = Ceramic Capacitor [capacitance=100nF package="100 mil [THT, multilayer]"]
  C2 = Ceramic Capacitor [capacitance=100nF package="100 mil [THT, multilayer]"]
  C3 = Ceramic Capacitor [capacitance=100nF package="100 mil [THT, multilayer]"]
  J1 = shrouded pin header, 10 pins [form="♂ (shrouded male)"]
  J2 = shrouded pin header, 10 pins [form="♂ (shrouded male)"]
  J3 = Screw terminal - 2 pins [package=THT]
  R1 = Resistor [tolerance=±5% resistance=150 package=THT]
  LED1 = LED - 5mm [color="Red (633nm)" package="5 mm [THT]"]
  R2 = Resistor [tolerance=±5% resistance=4.7k package=THT]
  J8 = male pin header, 3 pins [form="♂ (male)"]
  J7 = male pin header, 3 pins [form="♂ (male)"]
  J6 = male pin header, 3 pins [form="♂ (male)"]
  J4 = Screw terminal - 2 pins [package=THT]
  J5 = Screw terminal - 2 pins [package=THT]
  U1 = Voltage Regulator - 3.3V [package="TO220 [THT]"]
  C4 = Ceramic Capacitor [capacitance=0.1mF package="100 mil [THT, multilayer]"]
  R3 = Resistor [tolerance=±5% resistance=10k package=THT]
  R4 = Resistor [tolerance=±5% resistance=10k package=THT]
  C5 = Ceramic Capacitor [part_number=0.33mF package="100 mil [THT, multilayer]"]

nets:
  N1: IC1.GPB0, Q1.I1
  N2: IC1.GPB1, Q1.I2
  N3: IC1.GPB2, Q1.I3
  N4: IC1.GPB3, Q1.I4
  N5: IC1.GPB4, Q1.I5
  N6: IC1.GPB5, Q1.I6
  N7: IC1.GPB6, Q1.I7
  N8: IC1.GPB7, Q1.I8
  N9: IC1.VDD, C1.0, R2.Pin_0, J8.pin3, J7.pin3, J6.pin3, U1.output_voltage, C4.1, R3.Pin_1, R4.Pin_1
  GND: IC1.VSS, Q1.GND, Q2.GND, C1.1, C2.1, C3.1, J1.pin10, J2.pin10, J3.pin1, R1.Pin_0, J8.pin1, J7.pin1, J6.pin1, U1.GND, C4.0, C5.1
  N10: IC1.SCL, J4.pin2, J5.pin2, R4.Pin_0
  N11: IC1.SDA, J4.pin1, J5.pin1, R3.Pin_0
  N12: IC1.A0, J7.pin2
  N13: IC1.A1, J6.pin2
  N14: IC1.A2, J8.pin2
  N15: IC1.RESET, R2.Pin_1
  N16: IC1.GPA0, Q2.I1
  N17: IC1.GPA1, Q2.I2
  N18: IC1.GPA2, Q2.I3
  N19: IC1.GPA3, Q2.I4
  N20: IC1.GPA4, Q2.I5
  N21: IC1.GPA5, Q2.I6
  N22: IC1.GPA6, Q2.I7
  N23: IC1.GPA7, Q2.I8
  N24: Q1.COMMON, Q2.COMMON, C2.0, C3.0, J1.pin1, J2.pin1, J3.pin2, LED1.anode, U1.input_voltage, C5.0
  N25: Q1.O8, J1.pin9
  N26: Q1.O7, J1.pin8
  N27: Q1.O6, J1.pin7
  N28: Q1.O5, J1.pin6
  N29: Q1.O4, J1.pin5
  N30: Q1.O3, J1.pin4
  N31: Q1.O2, J1.pin3
  N32: Q1.O1, J1.pin2
  N33: Q2.O8, J2.pin9
  N34: Q2.O7, J2.pin8
  N35: Q2.O6, J2.pin7
  N36: Q2.O5, J2.pin6
  N37: Q2.O4, J2.pin5
  N38: Q2.O3, J2.pin4
  N39: Q2.O2, J2.pin3
  N40: Q2.O1, J2.pin2
  N41: R1.Pin_1, LED1.cathode

notes:
  Port A
  Port B
  SCL
  SDA
  I2C In
  I2C Out
  Addr1
  Addr2
  Addr3
  PWR
  5VDC 3.0A
  +
  -
  ULN2803
  MCP23017
  A0
  A1
  A2
  FAB 00101  ASSY 00102
  CLController I/O Expansion Module
  CLC-EXP Rev 1.1
  Copyright (c) 2022 Cyrus Brunner
  www.cyrusbuilt.net
  CLC-EXP, CLController I/O Expansion Module, 1.1
  5VDC 1.0A

custom parts:
  MCP23017 I2C I/O Expander: The MCP23017 uses two i2c pins (these can be shared with other i2c devices), and in exchange gives you 16 general purpose pins. You can set each of 16 pins to be input, output, input with a pullup or open drain. There's even the ability to get an interrupt via an external pin when any of the inputs change so you don't have to keep polling the chip.
  ULN2803 Darlington Array: ULN2803 Darlington Transistor Array with Flyback Protection
  Ceramic Capacitor: 0.33mf multilayer Ceramic Capacitor
