# Fritzing sketch RelayModule (saved by Fritzing 0.9.3b)
circuit board: 10.3588cm x 7.55617cm
breadboards: 2

parts:
  R9 = Resistor [tolerance=±5% resistance=150 package=THT]
  LED9 = LED - 5mm [color="Red (633nm)" package="5 mm [THT]"]
  J9 = shrouded pin header, 10 pins [form="♂ (shrouded male)"]
  U1 = RELAY [package=relay-jzc]
  U2 = RELAY [package=relay-jzc]
  U4 = RELAY [package=relay-jzc]
  U5 = RELAY [package=relay-jzc]
  J4 = Screw terminal - 2 pins [package=THT]
  J3 = Screw terminal - 2 pins [package=THT]
  J2 = Screw terminal - 2 pins [package=THT]
  J1 = Screw terminal - 2 pins [package=THT]
  LED5 = LED - 3mm [color="Green (570nm)" package="3 mm [THT]"]
  LED6 = LED - 3mm [color="Green (570nm)" package="3 mm [THT]"]
  LED7 = LED - 3mm [color="Green (570nm)" package="3 mm [THT]"]
  LED8 = LED - 3mm [color="Green (570nm)" package="3 mm [THT]"]
  R5 = Resistor [tolerance=±5% resistance=150 package=THT]
  R6 = Resistor [tolerance=±5% resistance=150 package=THT]
  R7 = Resistor [tolerance=±5% resistance=150 package=THT]
  R8 = Resistor [tolerance=±5% resistance=150 package=THT]
  R4 = Resistor [tolerance=±5% resistance=150 package=THT]
  R3 = Resistor [tolerance=±5% resistance=150 package=THT]
  LED4 = LED - 3mm [color="Green (570nm)" package="3 mm [THT]"]
  LED3 = LED - 3mm [color="Green (570nm)" package="3 mm [THT]"]
  LED2 = LED - 3mm [color="Green (570nm)" package="3 mm [THT]"]
  R2 = Resistor [tolerance=±5% resistance=150 package=THT]
  LED1 = LED - 3mm [color="Green (570nm)" package="3 mm [THT]"]
  R1 = Resistor [tolerance=±5% resistance=150 package=THT]
  U6 = RELAY [package=relay-jzc]
  J5 = Screw terminal - 2 pins [package=THT]
  J6 = Screw terminal - 2 pins [package=THT]
  U7 = RELAY [package=relay-jzc]
  J7 = Screw terminal - 2 pins [package=THT]
  U8 = RELAY [package=relay-jzc]
  J8 = Screw terminal - 2 pins [package=THT]
  U3 = RELAY [package=relay-jzc]

nets:
  N1: R9.Pin_0, J9.pin10, U1.COIL2, U2.COIL2, U4.COIL2, U5.COIL2, R5.Pin_1, R6.Pin_1, R7.Pin_1, R8.Pin_1, R4.Pin_0, R3.Pin_0, R2.Pin_0, R1.Pin_0, U6.COIL2, U7.COIL2, U8.COIL2, U3.COIL2
  N2: R9.Pin_1, LED9.cathode
  N3: LED9.anode, J9.pin1
  N4: J9.pin2, U1.COIL1, LED1.anode
  N5: J9.pin3, U2.COIL1, LED2.anode
  N6: J9.pin4, LED3.anode, U3.COIL1
  N7: J9.pin5, U4.COIL1, LED4.anode
  N8: J9.pin6, U5.COIL1, LED5.anode
  N9: J9.pin7, LED6.anode, U6.COIL1
  N10: J9.pin8, LED7.anode, U7.COIL1
  N11: J9.pin9, LED8.anode, U8.COIL1
  N12: U1.NO, J1.pin1
  N13: U1.MAIN, J1.pin2
  N14: U2.NO, J2.pin1
  N15: U2.MAIN, J2.pin2
  N16: U4.NO, J4.pin1
  N17: U4.MAIN, J4.pin2
  N18: U5.NO, J5.pin1
  N19: U5.MAIN, J5.pin2
  N20: J3.pin1, U3.NO
  N21: J3.pin2, U3.MAIN
  N22: LED5.cathode, R5.Pin_0
  N23: LED6.cathode, R6.Pin_0
  N24: LED7.cathode, R7.Pin_0
  N25: LED8.cathode, R8.Pin_0
  N26: R4.Pin_1, LED4.cathode
  N27: R3.Pin_1, LED3.cathode
  N28: LED2.cathode, R2.Pin_1
  N29: LED1.cathode, R1.Pin_1
  N30: U6.NO, J6.pin1
  N31: U6.MAIN, J6.pin2
  N32: U7.NO, J7.pin1
  N33: U7.MAIN, J7.pin2
  N34: U8.NO, J8.pin1
  N35: U8.MAIN, J8.pin2

notes:
  1
  2
  COM
  3
  4
  6
  5
  7
  8
  PWR
  FAB 00100 ASSY 00101
  CLCRM, CLController Relay Module.     Designer: Cyrus Brunner, 1.0
  +5V DC
  REL 1
  REL 2
  OUT 1
  OUT 2
  OUT 3
  OUT 4
  OUT 5
  OUT 6
  OUT 7
  OUT 8
  REL 3
  REL 4
  REL 5
  REL 8
  REL 7
  REL 6
  CLCRM Rev 1.0
  Copyright (c) 2020 Cyrus Brunner
  www.cyrusbuilt.net
  CLController Relay Module
